// Logisim project mips_processor.circ as structural Verilog
module ALU (
  input  [31:0] R1,
  input  [31:0] R2,
  input  [5:0] Funct,
  input  [1:0] ALUOp,
  output C_Out,
  output [31:0] out_6,
  output B_Out,
  output Zero
);

  wire comparator_1_lt, or_2_out;
  wire [3:0] ALU_Control, R_Format;
  wire [31:0] adder_1_out, and_1_out, bit_extender_1_out, or_1_out, signal;

  Multiplexer #(.select(4), .width(4)) multiplexer_1 (
    .in0(4'b0010), .in1(4'b0110), .in4(4'b0000), .in5(4'b0001), .in10(4'b0111), .out(R_Format),
    .sel(Funct[5:2]), .en(1'b1));  // open: in2, in3, in6, in7, in8, in9, in11, in12, in13, in14, in15
  assign and_1_out = R1 & R1;  // AND_Gate and_1, 32 bits wide
  assign or_1_out = R1 | R1;  // OR_Gate or_1, 32 bits wide
  Subtractor #(.width(32)) subtractor_1 (.a(R1), .b(R2), .out(signal), .bin(1'b0), .bout(B_Out));
  Comparator #(.width(32)) comparator_1 (.a(R1), .b(R2), .lt(comparator_1_lt));  // open: gt, eq
  Adder #(.width(32)) adder_1 (.a(R1), .b(R2), .out(adder_1_out), .cin(1'b0), .cout(C_Out));
  assign bit_extender_1_out = {{31{1'b0}}, comparator_1_lt};  // Bit_Extender bit_extender_1
  Multiplexer #(.select(2), .width(4)) multiplexer_2 (
    .in0(4'b0010), .in1(4'b0110), .in2(R_Format), .out(ALU_Control), .sel(ALUOp), .en(1'b1));  // open: in3
  Multiplexer #(.select(4), .width(32)) multiplexer_3 (
    .in0(and_1_out), .in1(or_1_out), .in2(adder_1_out), .in6(signal), .in7(bit_extender_1_out), .out(out_6),
    .sel(ALU_Control), .en(1'b1));  // open: in3, in4, in5, in8, in9, in10, in11, in12, in13, in14, in15
  or or_2 (or_2_out, signal[0], signal[1], signal[2], signal[3], signal[4], signal[5], signal[6], signal[7], signal[8], signal[9], signal[10], signal[11], signal[12], signal[13], signal[14], signal[15], signal[17], signal[18], signal[19], signal[20], signal[21], signal[22], signal[23], signal[24], signal[25], signal[26], signal[27], signal[28], signal[29], signal[30], signal[31], signal[16]);
  not not_1 (Zero, or_2_out);
endmodule
